# Fritzing sketch final_fritzing (saved by Fritzing 1.0.4)
breadboards: 1

parts:
  U1 = WS2812 RGB LED matrix 1x8
  Mod1 = ESP32-TTGO-T-DISPLAY
  Part1 = Breakout Board for Electret Microphone
  R1 = Resistor [tolerance=±5% power=0.25W resistance=220 package=THT]

nets:
  GND: U1.GND, Mod1.G-1, Mod1.G-2, Mod1.G-10, Mod1.G-11, Mod1.G-14, Part1.GND
  VCC: U1.VCC, Mod1.3V, Part1.VCC
  N1: U1.DIN, R1.Pin_1
  N2: Mod1.17, R1.Pin_0
  N3: Mod1.2, Part1.AUD

custom parts:
  WS2812 RGB LED matrix 1x8: WS2812 matrix 1x8
  ESP32-TTGO-T-DISPLAY: LILYGO TTGO T-Display GD32VF103CBT6 Main Chip ST7789 1.14 Inch IPS 240x135 Resolution Minimalist Development Board.
